# Fritzing sketch SmartFarm (saved by Fritzing 1.0.6)

parts:
  M1 = DOIT Esp32 DevKit v1 (30 pins long, 11 pins width) [part_number=ESP32S-PIN30]
  S1 = Pushbutton [package="[THT]"]
  S2 = Pushbutton [package="[THT]"]
  S3 = Pushbutton [package="[THT]"]
  Linh_kiện1 = Soil Moisture Sensor
  HC-SR04_Sensor_1 = HC-SR04 Ultrasonic Distance Sensor
  SERVO1 = Tower Pro SG90 servo [part_number=101246]
  DHT1 = DHT11 Humitidy and Temperature Sensor
  Sensor1 = Gas Sensor Breakout Board
  S4 = KY-026
  A1 = PIR sensor (non-bendable legs)
  Mod1 = Passive Buzzer
  U1 = RFID RC522 SIP - 8 pins [chip_label="RFID RC522" package="SIP (Single Inline) [THT]"]
  Mod2 = KY-018 Photoresistor Module [package="Breakout board"]
  U2 = 2-Channel 5v Relay Shield [package=relay-2ch5v10a]
  F1 = Fan - Ventilador [package=THT]
  Mini_Water_Pump_3-6VDC1 = Mini Water Pump 3-6VDC [part_number="Mini Water Pump 3-6VDC" chip_label=IC package="DIP (Dual Inline) [THT]"]
  R2 = Resistor [tolerance=±5% power=0.25W resistance=220 package=THT]
  LED1 = LED - 5mm [color="Red (633nm)" current=0.030A package="5 mm [THT]"]

nets:
  3.3V: M1.3V3, Linh_kiện1.VCC, DHT1.VDD, S4.pin3, U1.VCC, Mod2.Vin
  GND: M1.GND, S1.Pin_1, S1.Pin_2, S2.Pin_1, S2.Pin_2, S3.Pin_1, S3.Pin_2, Linh_kiện1.GND, HC-SR04_Sensor_1.GND, SERVO1.GND, DHT1.GND, Sensor1.GND, S4.pin2, A1.GND, Mod1.S, U1.GND, Mod2.-, LED1.cathode
  N1: M1.D2, R2.Pin_0
  N2: M1.D4, DHT1.DATA
  N3: M1.RX2, U2.IN1
  N4: M1.TX2, U2.IN2
  N5: M1.D5, U1.NSS
  N6: M1.D18, U1.SCK
  N7: M1.D19, U1.MISO
  N8: M1.D21, Mod1.NC
  N9: M1.D22, U1.RST
  N10: M1.D23, U1.MOSI
  N11: M1.VP, S3.Pin_4
  N12: M1.D34, Linh_kiện1.SIG
  N13: M1.D35, Sensor1.AOUT
  N14: M1.D32, S2.Pin_4
  N15: M1.D33, S1.Pin_4
  N16: M1.D25, SERVO1.Signal
  N17: M1.D26, Mod2.S
  N18: M1.D27, S4.pin4
  N19: M1.D14, A1.SIG
  N20: M1.D12, HC-SR04_Sensor_1.TRIG
  N21: M1.D13, HC-SR04_Sensor_1.ECHO
  5V: M1.VIN, HC-SR04_Sensor_1.VCC, SERVO1.+5V, Sensor1.5V, A1.VDD, Mod1.-
  N22: U2.GND, U2.JD-GND
  N23: U2.K1-Off, F1.5V
  N24: U2.K1-On, F1.GND
  N25: U2.K2-Off, Mini_Water_Pump_3-6VDC1.+M
  N26: U2.K2-On, Mini_Water_Pump_3-6VDC1.-M
  N27: R2.Pin_1, LED1.anode

custom parts:
  DOIT Esp32 DevKit v1 (30 pins long, 11 pins width): The DOIT Esp32 DevKit v1 is one of the development board created by DOIT to evaluate the ESP-WROOM-32 module. It is based on the ESP32 microcontroller that boasts Wifi, Bluetooth, Ethernet and Low Power support all in a single chip. (vanepp) made breadboard work, adjusted pin numbering and labels and reduced size of schematic and cleaned up pcb. This chip is 30pins long (2 x15) and 11 pins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
  Tower Pro SG90 servo: Original file by John De Cristofaro http://www.adafruit.com/products/1449 Adafruit Feedback Servo (Small) Edited by: e-radionica.com 28/9/2015
  DHT11 Humitidy and Temperature Sensor: DHT11 Humidity and Temperature Sensor
  Gas Sensor Breakout Board: Gas sensor breakout board. Input voltage is 5V. Sensor output is available in analog and digital.
  KY-026: ky-026 flame sensor module
  PIR sensor (non-bendable legs): Generic PIR sensor
  RFID RC522 SIP - 8 pins: A SIP stand-in part for RFID RC522 . With 8 pins on a 300 mil single inline package (SIP) footprint.
  KY-018 Photoresistor Module: KY-018 Photoresistor module, used to measure light intensity. It can determine the presence or absence of light.
  2-Channel 5v Relay Shield: 2 Channel 5v Relay Shield w. 2x SPD-06VDC-SD-C
  Fan - Ventilador: Ventilador de 2 pines, se encuentra comunmente en computadoras de escritorio
